# Fritzing sketch Trolly-1 (saved by Fritzing 0.9.3b)

parts:
  Part1 = Arduino Uno (Rev3)
  Bluetooth_Module = Bluetooth HC-05 Macho
  Right_Ultra_Sonic = hc-sr04
  12v_power = Power plug
  M4 = L293D Motor Driver
  Left_Ultra_Sonic = hc-sr04
  Center_Ultra_Sonic = hc-sr04
  M6 = DC Motor
  M5 = DC Motor
  S5 = SPST Switch [package=r_sw_th]

nets:
  N1: Part1.D8, Right_Ultra_Sonic.Echo
  N2: Part1.D9_PWM, Right_Ultra_Sonic.Trig
  N3: Part1.D10_PWM/SS, Left_Ultra_Sonic.Echo
  N4: Part1.D11_PWM/MOSI, Left_Ultra_Sonic.Trig
  N5: Part1.D12/MISO, Center_Ultra_Sonic.Echo
  N6: Part1.D13/SCK, Center_Ultra_Sonic.Trig
  N7: Part1.D2, Bluetooth_Module.TXD
  N8: Part1.D3_PWM, Bluetooth_Module.RXD
  N9: Part1.D4, M4.pin_8
  N10: Part1.D5_PWM, M4.pin_7
  N11: Part1.D6_PWM, M4.pin_6
  N12: Part1.D7, M4.pin_5
  VCC: Part1.5V, Right_Ultra_Sonic.VCC, Left_Ultra_Sonic.VCC, Center_Ultra_Sonic.VCC
  GND: Part1.GND, Bluetooth_Module.GND, Right_Ultra_Sonic.GND, M4.pin_4, Left_Ultra_Sonic.GND, Center_Ultra_Sonic.GND
  N13: Bluetooth_Module.VCC, M4.pin_3
  N14: 12v_power.VCC, S5.O
  N15: M4.pin_9, M5.pin_1
  N16: M4.pin_10, M5.pin_2
  N17: M4.pin_11, M6.pin_1
  N18: M4.pin_12, M6.pin_2
